# Fritzing sketch currentsource_mod (saved by Fritzing 0.9.2b)
circuit board: 5cm x 2cm
breadboards: 1

parts:
  I_out- = Header 1 [package=1x01_offset]
  I_out+ = Header 1 [package=1x01_offset]
  V_pwr+ = Header 1 [package=1x01_offset]
  GND_pwr = Header 1 [package=1x01_offset]
  I_set = Header 1 [package=1x01_offset]
  V_ctl = Header 1 [package=1x01_offset]
  GND_ctrl = Header 1 [package=1x01_offset]
  PWM = Header 1 [package=1x01_offset]
  R3 = Resistor [tolerance=±5% resistance=100k package="1206 [SMD]"]
  Rpwm1 = Resistor [tolerance=±5% resistance=1k package="1206 [SMD]"]
  Rmosfet1 = Resistor [tolerance=±5% resistance=100 package="1206 [SMD]"]
  Rsense = Resistor [tolerance=±5% resistance=0.1 power=2W package="2010 [SMD]"]
  Rpwm2 = Resistor [tolerance=±5% resistance=100k power=2W package="1206 [SMD]"]
  Risetfilter = Resistor [tolerance=±5% resistance=100k package="1206 [SMD]"]
  NPNpwm = NPN-Transistor [package="SOT-23 [SMD]"]
  NCHANpwr = Basic FET N-Channel [package="D2Pak [SMD]"]
  C1 = Capacitor [package=0805]
  OPAMP1 = Dual Op-Amp [package=so08]

nets:
  N1: I_out-.1, NCHANpwr.drain
  N2: I_out+.1, V_pwr+.1
  N3: GND_pwr.1, GND_ctrl.1, Rsense.Pin_1, Rpwm2.Pin_1, NPNpwm.2, C1.2, OPAMP1.A_V-
  N4: I_set.1, Risetfilter.Pin_0
  N5: V_ctl.1, OPAMP1.A_V+
  N6: PWM.1, Rpwm1.Pin_0, Rpwm2.Pin_0
  N7: R3.Pin_0, OPAMP1.A_OUT, OPAMP1.A_-IN
  N8: R3.Pin_1, NPNpwm.1, OPAMP1.B_+IN
  N9: Rpwm1.Pin_1, NPNpwm.0
  N10: Rmosfet1.Pin_0, OPAMP1.B_OUT
  N11: Rmosfet1.Pin_1, NCHANpwr.Gate
  N12: Rsense.Pin_0, NCHANpwr.source, OPAMP1.B_-IN
  N13: Risetfilter.Pin_1, C1.1, OPAMP1.A_+IN
